# Fritzing sketch OBC+SB (saved by Fritzing 0.9.9b)
breadboards: 2

parts:
  U1 = microSD Socket [package="Molex 502774-0891 [SMD]"]  # not connected
  Raspberry_Pi_1 = Raspberry Pi 3 [part_number=RPI-3-V1.2]
  J4 = shrouded pin header, 40 pins [form="♂ (shrouded male)"]
  Part7 = Arduino Pro Mini v13
  Part8 = Humidity Temperature Sensor SHT15
  Part9 = Triple Axis Magnetometer - HMC5883 Breakout

nets:
  N1: Raspberry_Pi_1.GPIO2, J4.pin20, Part7.A4, Part8.SDA, Part9.SDA
  N2: Raspberry_Pi_1.GPIO3, J4.pin19, Part7.A5, Part8.SCL, Part9.SCL
  N3: Raspberry_Pi_1.GPIO23, Raspberry_Pi_1.GND, J4.pin26
  N4: Raspberry_Pi_1.GPIO18, Raspberry_Pi_1.GPIO15, J4.pin17, Part7.D1/RX
  N5: Raspberry_Pi_1.GPIO14, J4.pin18, Part7.D0/TX
  N6: Raspberry_Pi_1.5V, J4.pin16
  VCC: J4.pin12, Part7.VCC, Part8.VCC, Part9.VCC
  GND: Part7.GND, Part8.GND, Part9.GND

notes:
  UniSat BUS
  UniSat OBC Analogy on the Fritzing (v1.0 by @azataiot)
  BLACK-GND
  RED-PWR
  YELLOW - I2C SDA
  GREEN - I2C SDL
  WHITE* - RS485 A
  ORANGE* - RS485 B
