# Fritzing sketch OBC (saved by Fritzing 0.9.9b)
breadboards: 1

parts:
  U1 = microSD Socket [package="Molex 502774-0891 [SMD]"]  # not connected
  Raspberry_Pi_1 = Raspberry Pi 3 [part_number=RPI-3-V1.2]
  J4 = shrouded pin header, 40 pins [form="♂ (shrouded male)"]

nets:
  N1: Raspberry_Pi_1.GPIO2, J4.pin20
  N2: Raspberry_Pi_1.GPIO3, J4.pin19
  N3: Raspberry_Pi_1.GPIO23, Raspberry_Pi_1.GND, J4.pin26
  N4: Raspberry_Pi_1.GPIO18, Raspberry_Pi_1.GPIO15, J4.pin17
  N5: Raspberry_Pi_1.GPIO14, J4.pin18
  N6: Raspberry_Pi_1.5V, J4.pin16

notes:
  UniSat BUS
  UniSat OBC Analogy on the Fritzing (v1.0 by @azataiot)
  BLACK-GND
  RED-PWR
  YELLOW - I2C SDA
  GREEN - I2C SDL
  WHITE* - RS485 A
  ORANGE* - RS485 B
