# Fritzing sketch SB (saved by Fritzing 0.9.9b)
breadboards: 1

parts:
  J5 = shrouded pin header, 40 pins [form="♂ (shrouded male)"]
  Part4 = Triple Axis Magnetometer - HMC5883 Breakout
  Part5 = Humidity Temperature Sensor SHT15
  Part6 = Arduino Pro Mini v13

nets:
  VCC: J5.pin11, Part4.VCC, Part5.VCC, Part6.VCC
  N1: J5.pin17, Part6.D1/RX
  N2: J5.pin18, Part6.D0/TX
  N3: J5.pin19, Part4.SCL, Part6.A5
  N4: J5.pin20, Part4.SDA, Part5.SDA, Part6.A4
  N5: J5.pin30, Part6.GND
  GND: Part4.GND, Part5.GND

notes:
  UniSat BUS
  UniSat SB Analogy on the Fritzing (v1.0 by @azataiot)
  BLACK-GND
  RED-PWR
  YELLOW - I2C SDA
  GREEN - I2C SDL
  WHITE* - RS485 A
  ORANGE* - RS485 B
